# Fritzing sketch Supplemental_File_13_DC_motor_controller_interface22 (saved by Fritzing 0.9.3b)
circuit board: 8.46667cm x 5.64444cm
breadboards: 1

parts:
  U2 = ATTINY45 [part_number=attiny85 package=dip]
  C1 = Electrolytic Capacitor [capacitance=10µF package="0405 [SMD, electrolytic]"]
  R4 = Resistor [tolerance=±5% resistance=1k package=THT]
  R5 = Resistor [tolerance=±5% resistance=1k package=THT]
  R6 = Resistor [tolerance=±5% resistance=10k package=THT]
  R8 = Resistor [tolerance=±5% resistance=10k package=THT]
  R9 = Resistor [tolerance=±5% resistance=10k package=THT]
  R10 = Resistor [tolerance=±5% resistance=1k package=THT]
  U3 = DIODE-ZENER [part_number="removed from Tunze DC controller" package=diode-zener]  # not connected
  U1 = Optocoupler [part_number=MCT2E package=THT]

nets:
  N1: U2.PB3(ADC3), R9.Pin_1, R10.Pin_0
  N2: U2.GND, C1.-, R6.Pin_0, R9.Pin_0
  N3: U2.PB2(SCK_ADC1), R4.Pin_1, R6.Pin_1
  N4: U2.VCC, C1.+, U1.Pin_5
  N5: R4.Pin_0, U1.Pin_4
  N6: R5.Pin_1, R8.Pin_0, U1.Pin_1
  N7: R8.Pin_1, U1.Pin_2

notes:
  connected to Tunze
  DC motor controller
  (distal diode pad)
  (30 gage wire)
  connected to Tunze
  DC motor controller
  ATMEL pin 3
  (= proximal diode pad)
  (30 gage wire)
  connected to Tunze
  motor controller
  +5 VDC
  (30 gage wire)
  connected to Tunze
  motor controller
  GND
  (30 gage wire)
  connected to Walchem controller output (Relay 7)
  (HIGH during feeding cycle)
  Zener Diode is the surface mount component removed from the Tunze control board padsmiconductoer
  Optocoupler is MCT2E
  (ON Semiconductor)
  ATtiny 85 is programmed using Arduino IDE (see associated program file)
  Controller circuit to interrupt the Tunze protein skimmer DC motor controller. Dr. J. Henry (UIUC)
