# Fritzing sketch Supplemental_File_13_Peristaltic pump controller (saved by Fritzing 0.9.3b)
breadboards: 1

parts:
  Part1 = Arduino Uno (Rev3)
  U4 = LCD-16X2 [package=lcd-16x2_noholes]  # not connected
  BUTTON1 = Waterproof Pushbutton (green)
  M1 = Stepper Motor - Bipolar
  Part2 = Adafruit DRV8833 DC/Stepper Motor Driver [part_number="Adafruit #3297"]
  Part3 = Adafruit Analog 2-Axis Joystick [part_number="Adafruit #512"]
  R1 = Resistor [tolerance=±5% resistance=10k package=THT]

nets:
  N1: Part1.A0, Part3.YOUT
  N2: Part1.A1, Part3.XOUT
  N3: Part1.D8, Part2.AIN1
  N4: Part1.D9_PWM, Part2.AIN2
  N5: Part1.D10_PWM/SS, Part2.BIN2
  N6: Part1.D11_PWM/MOSI, Part2.BIN1
  N7: Part1.D13/SCK, Part2.!SLEEP
  N8: Part1.D2, R1.Pin_0
  N9: Part1.D7, Part3.SWITCH
  5V: Part1.5V, BUTTON1.no_name_yet#4, Part3.VCC
  GND: Part1.GND, BUTTON1.no_name_yet#5, Part2.GND, Part3.GND, R1.Pin_1
  N10: Part1.VIN, Part2.VMOTOR
  N11: M1.A, Part2.BOUT1
  N12: M1.C, Part2.BOUT2
  N13: M1.B, Part2.AOUT2
  N14: M1.D, Part2.AOUT1

notes:
  Arduino Uno. To insure enough power to the motor, use 9VDC power supply.
  Main power button and system power staus light. Cut trace on back of Uno's barrel jack to connect switch
  Input from feeding controller (goes HIGH) to trigger the pumping program (to Interrupt pin A0).
  10k resister insures pin does not float
  LCD, Display with Serial Backpack
  Adafruit, ID 782
  Joytick for entering values for speed (rpm) and volume (steps). Button (Sel) pin enters values into eeprom
  This circuit is a peristaltic pump controller. Values for speed (steps per min or rpm) and the number of steps (volume) can be entered and stored permantly in eeprom, and recalled as needed. Interrupt pin A0 (digital pin 2) is used to recieve input from the Feeding Controller to trigger a pumping cycle.
  J.J. Henry, UIUC, Dec. 9 2019
  Peristaltic Pump Stepper motor, 200 steps. 5-12 VDC. Note some wires may need to be swapped to obtain correct direction of rotation.
  Adafruit DRV8833
  Stepper Motor Driver. Input voltage to motors is 9 VDC from Uno's VIN pin

custom parts:
  Waterproof Pushbutton (green): Waterproof Illuminated Pushbutton (green)
  Adafruit DRV8833 DC/Stepper Motor Driver: Spin two DC motors or step one bi-polar or uni-polar stepper with up to 1.2A per channel using the DRV8833. This motor driver chip is a nice alternative to the TB6612 driver. Like that chip, you get 2 full H-bridges, but this chip is better for low voltage uses (can run from 2.7V up to 10.8V motor power) and has built in current limiting capability. We set it up for 1A current limiting so you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
  Adafruit Analog 2-Axis Joystick: This mini-kit makes it easy to mount a PSP/Xbox-like thumb joystick to your project. The thumbstick is an analog joystick - more accurate and sensitive than just 'directional' joysticks - with a 'press in to select' button. Since it's analog, you'll need two analog reading pins on your microcontroller to determine X and Y. Having an extra digital input will let you read the switch. The pack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
