# Fritzing sketch Supplemental_File_4_Feeding_controller2 (saved by Fritzing 0.9.3b)
breadboards: 1

parts:
  Part1 = Arduino Uno (Rev3)  # not connected
  Part3 = Adafruit DS1307 RTC Breakout [part_number="Adafruit #264"]
  U2 = Optocoupler [part_number=MCT2E package=THT]
  IR1 = TSOP312.., 314.. [part_number=TSOP1839 package=THT]
  R1 = Resistor [tolerance=±5% resistance=2.2k package=THT]
  U3 = LCD-16X2 [part_number="Adafruit LCD display with serial backpack" package=lcd-16x2_noholes]  # not connected
  R2 = Resistor [tolerance=±5% resistance=1k package=THT]
  R3 = Resistor [tolerance=±5% resistance=1k package=THT]
  2_Channel_Relay1 = 2 Channel Power Relay [part_number="Dual relay control board"]
  U4 = Optocoupler [part_number=MCT2E package=THT]
  LED2 = LED - 5mm [color="Red (633nm)" package="5 mm [THT]"]
  LED3 = LED - 5mm [color="Green (565nm)" package="5 mm [THT]"]
  LED4 = LED - 5mm [color="Blue (505nm)" package="5 mm [THT]"]
  R4 = Resistor [tolerance=±5% resistance=220 package=THT]
  R5 = Resistor [tolerance=±5% resistance=220 package=THT]
  R6 = Resistor [tolerance=±5% resistance=220 package=THT]
  LED1 = LED - 5mm [color="Infrared (880nm)" package="5 mm [THT]"]
  R7 = Resistor [tolerance=±5% resistance=1k package=THT]
  R10 = Resistor [tolerance=±5% resistance=1k package=THT]
  Ethernet_Sheild = Arduino Ethernet Shield (Rev3)
  R11 = Resistor [tolerance=±5% resistance=10k package=THT]
  R12 = Resistor [tolerance=±5% resistance=10k package=THT]

nets:
  N1: Part3.SCL, Ethernet_Sheild.A4/SDA
  N2: Part3.SDA, Ethernet_Sheild.A5/SCL
  VCC: Part3.VCC, IR1.Vs, 2_Channel_Relay1.VCC#14, R4.Pin_0, R5.Pin_0, R6.Pin_0, Ethernet_Sheild.5V
  GND: Part3.GND, U2.Pin_2, IR1.GND, 2_Channel_Relay1.GND, U4.Pin_2, LED1.cathode, Ethernet_Sheild.GND, R11.Pin_0, R12.Pin_0
  N3: U2.Pin_1, R3.Pin_0, R12.Pin_1
  N4: U2.Pin_5, R7.Pin_0
  N5: IR1.Data, Ethernet_Sheild.D7
  N6: R1.Pin_0, Ethernet_Sheild.SDCS
  N7: R1.Pin_1, LED1.anode
  N8: R2.Pin_0, U4.Pin_1, R11.Pin_1
  N9: R2.Pin_1, Ethernet_Sheild.PWM_D9
  N10: R3.Pin_1, Ethernet_Sheild.D8
  N11: 2_Channel_Relay1.JD-VCC, 2_Channel_Relay1.VCC#9
  N12: 2_Channel_Relay1.IN1, Ethernet_Sheild.PWM_D6
  N13: 2_Channel_Relay1.IN2, Ethernet_Sheild.PWM_D5
  N14: 2_Channel_Relay1.K1-COM, 2_Channel_Relay1.K2-COM
  N15: U4.Pin_5, R10.Pin_0
  N16: LED2.cathode, R4.Pin_1
  N17: LED2.anode, Ethernet_Sheild.A2
  N18: LED3.cathode, R6.Pin_1
  N19: LED3.anode, Ethernet_Sheild.A0
  N20: LED4.cathode, R5.Pin_1
  N21: LED4.anode, Ethernet_Sheild.A1

notes:
  Exploded view showing Ethernet sheild, which would normally sit on top of the Arduino Uno
  jumper
  Note: white tx wire must be disconnected before programing the arduino uno or the LCD display parameters may become corrupted,
  and those would need to be re-programmed)
  Real Time Clock
  (Adafruit, see parts )
  Dual Relay Control Board
  System Status LEDs and resistors are located within the main power switch
  (Adafruit, see parts list)
  Connections to PNP capacitance 3 wire sensor (per colors, by universal code)
  LCD Display with serial Backpack
  (Adafruit, ID 782, see parts )
  Connections to peristaltic pump controller, 5VDC and trigger (pin 2) = Pins 1 and 2, as used on DB9 connector, respectively
  Connections to aquarium system Walhem controller's input D5 for bypass valve: 12VDC and trigger. Note a 1K resistor is added, in series inside the Walchem controller on this orange wire
  Food Sensor:
  Infrared LED and TSOP1839 sensor
  120 VAC Hot Line voltage in
  120 VAC to Stir plate
  120 VAC to Air pump
  MCT2E Optocouplers for electrical isolation
  Automated Feeding Controller
  This circuit is modified from the original, now for use with the peristatlic pump controller
  Dr. J. Henry (UIUC) Dec 9, 2019.
  Note: Add a main power button with internal system power staus lights (LEDs shown here). Cut trace on back of Uno's barrel jack to connect on/ioff power switch (Not shown here, see parts list).
  Essential common AC and GND connections not shown here

custom parts:
  Adafruit DS1307 RTC Breakout: This is a great battery-backed real time clock (RTC) that allows your microcontroller project to keep track of time even if it is reprogrammed, or if the power is lost. Perfect for datalogging, clock-building, time stamping, timers and alarms, etc. The DS1307 is the most popular RTC - but it requires 5V power to work (although we've used it with 5V power and 3.3V logic successfully) PCB &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
  2 Channel Power Relay: A 2 channel power relay. The module operates at 5V.
